// Logisim project CTR.circ as structural Verilog: 8 circuits, main circuit main
module main (
  input  CLK,
  input  RST,
  output A,
  output B,
  output C,
  output D,
  output E,
  output F,
  output G,
  output SEL
);

  wire and_1_out, custom_counter_10_1_ovf, d_ff_1_qn, d_ff_2_qn, d_ff_3_qn, d_ff_4_qn, d_ff_5_qn;
  wire [1:0] d_ff_4_q;
  wire [2:0] full_counter_1_s_tens;
  wire [3:0] full_counter_1_m_ones, full_counter_1_m_tens, full_counter_1_s_ones, multiplexer_1_out;

  and and_1 (and_1_out, CLK, RST);
  D_Flip_Flop d_ff_1 (.D(d_ff_1_qn), .clk(CLK), .Qn(d_ff_1_qn), .reset(and_1_out));  // open: Q, preset
  D_Flip_Flop d_ff_2 (.D(d_ff_2_qn), .clk(d_ff_1_qn), .Qn(d_ff_2_qn), .reset(and_1_out));  // open: Q, preset
  D_Flip_Flop d_ff_3 (.D(d_ff_3_qn), .clk(d_ff_2_qn), .Q(SEL), .Qn(d_ff_3_qn), .reset(and_1_out));  // open: preset
  D_Flip_Flop d_ff_4 (
    .D(d_ff_4_qn), .clk(d_ff_3_qn), .Q(d_ff_4_q[0]), .Qn(d_ff_4_qn), .reset(and_1_out));  // open: preset
  D_Flip_Flop d_ff_5 (
    .D(d_ff_5_qn), .clk(d_ff_4_qn), .Q(d_ff_4_q[1]), .Qn(d_ff_5_qn), .reset(and_1_out));  // open: preset
  custom_counter_10 custom_counter_10_1 (.CLK(CLK), .RST(and_1_out), .OVF(custom_counter_10_1_ovf));  // open: COUNT
  full_counter full_counter_1 (
    .RST(and_1_out), .CLK(custom_counter_10_1_ovf), .FCLK(CLK), .S_ONES(full_counter_1_s_ones),
    .S_TENS(full_counter_1_s_tens), .M_ONES(full_counter_1_m_ones), .M_TENS(full_counter_1_m_tens));
  Multiplexer #(.select(2), .width(4)) multiplexer_1 (
    .in0(full_counter_1_s_ones), .in1({1'b0, full_counter_1_s_tens}), .in2(full_counter_1_m_ones),
    .in3(full_counter_1_m_tens), .out(multiplexer_1_out), .sel(d_ff_4_q));
  bcd_to_seg bcd_to_seg_1 (.BCD(multiplexer_1_out), .A(A), .B(B), .C(C), .D(D), .E(E), .F(F), .G(G));
endmodule

module seconds_counter (
  input  RST,
  input  CLK,
  input  FCLK,
  output [3:0] ONES,
  output [2:0] TENS,
  output OVF
);

  wire comparator_1_eq, comparator_2_eq, d_ff_1_q, not_1_out, or_1_out, or_2_out;

  not not_1 (not_1_out, FCLK);
  or or_1 (or_1_out, RST, d_ff_1_q);
  or or_2 (or_2_out, RST, OVF);
  D_Flip_Flop d_ff_1 (.D(comparator_1_eq), .clk(not_1_out), .Q(d_ff_1_q));  // open: Qn, preset, reset
  custom_counter_4 custom_counter_4_1 (.CLK(CLK), .RST(or_1_out), .COUNT(ONES));
  custom_counter_3 custom_counter_4_2 (.CLK(d_ff_1_q), .RST(or_2_out), .COUNT(TENS));
  D_Flip_Flop d_ff_2 (.D(comparator_2_eq), .clk(not_1_out), .Q(OVF));  // open: Qn, preset, reset
  Comparator #(.mode("unsigned"), .width(4)) comparator_1 (
    .a(ONES), .b(4'b1010), .eq(comparator_1_eq));  // open: gt, lt
  Comparator #(.mode("unsigned"), .width(3)) comparator_2 (.a(TENS), .b(3'b110), .eq(comparator_2_eq));  // open: gt, lt
endmodule

module full_counter (
  input  RST,
  input  CLK,
  input  FCLK,
  output [3:0] S_ONES,
  output [2:0] S_TENS,
  output [3:0] M_ONES,
  output [3:0] M_TENS
);

  wire comparator_1_eq, comparator_2_eq, d_ff_1_q, d_ff_2_q, not_1_out, or_1_out, or_2_out,
       seconds_counter_1_ovf;

  not not_1 (not_1_out, FCLK);
  or or_1 (or_1_out, RST, d_ff_1_q);
  D_Flip_Flop d_ff_1 (.D(comparator_1_eq), .clk(not_1_out), .Q(d_ff_1_q));  // open: Qn, preset, reset
  or or_2 (or_2_out, RST, d_ff_2_q);
  D_Flip_Flop d_ff_2 (.D(comparator_2_eq), .clk(not_1_out), .Q(d_ff_2_q));  // open: Qn, preset, reset
  custom_counter_4 custom_counter_4_1 (.CLK(seconds_counter_1_ovf), .RST(or_1_out), .COUNT(M_ONES));
  custom_counter_4 custom_counter_4_2 (.CLK(d_ff_1_q), .RST(or_2_out), .COUNT(M_TENS));
  seconds_counter seconds_counter_1 (
    .RST(RST), .CLK(CLK), .FCLK(FCLK), .ONES(S_ONES), .TENS(S_TENS), .OVF(seconds_counter_1_ovf));
  Comparator #(.mode("unsigned"), .width(4)) comparator_1 (
    .a(M_ONES), .b(4'b1010), .eq(comparator_1_eq));  // open: gt, lt
  Comparator #(.mode("unsigned"), .width(4)) comparator_2 (
    .a(M_TENS), .b(4'b1010), .eq(comparator_2_eq));  // open: gt, lt
endmodule

module bcd_to_seg (
  input  [3:0] BCD,
  output A,
  output B,
  output C,
  output D,
  output E,
  output F,
  output G
);

  ROM #(.addrWidth(4), .dataWidth(7)) ROM_1 (.addr(BCD), .data({G, F, E, D, C, B, A}));

  // Notes on the sheet:
  //   contents of ROM_1 (hex, n*v repeats v):
  //   3f 6 5b 4f 66 6d 7d 7 7f 6f
endmodule

module custom_counter_10 (
  input  CLK,
  input  RST,
  output [9:0] COUNT,
  output OVF
);

  wire d_ff_1_qn, d_ff_2_qn, d_ff_3_qn, d_ff_4_qn, d_ff_5_qn, d_ff_6_qn, d_ff_7_qn, d_ff_8_qn, d_ff_9_qn;

  D_Flip_Flop d_ff_1 (.D(d_ff_1_qn), .clk(CLK), .Q(COUNT[0]), .Qn(d_ff_1_qn), .reset(RST));  // open: preset
  D_Flip_Flop d_ff_2 (.D(d_ff_2_qn), .clk(d_ff_1_qn), .Q(COUNT[1]), .Qn(d_ff_2_qn), .reset(RST));  // open: preset
  D_Flip_Flop d_ff_3 (.D(d_ff_3_qn), .clk(d_ff_2_qn), .Q(COUNT[2]), .Qn(d_ff_3_qn), .reset(RST));  // open: preset
  D_Flip_Flop d_ff_4 (.D(d_ff_4_qn), .clk(d_ff_3_qn), .Q(COUNT[3]), .Qn(d_ff_4_qn), .reset(RST));  // open: preset
  D_Flip_Flop d_ff_5 (.D(d_ff_5_qn), .clk(d_ff_4_qn), .Q(COUNT[4]), .Qn(d_ff_5_qn), .reset(RST));  // open: preset
  D_Flip_Flop d_ff_6 (.D(d_ff_6_qn), .clk(d_ff_5_qn), .Q(COUNT[5]), .Qn(d_ff_6_qn), .reset(RST));  // open: preset
  D_Flip_Flop d_ff_7 (.D(d_ff_7_qn), .clk(d_ff_6_qn), .Q(COUNT[6]), .Qn(d_ff_7_qn), .reset(RST));  // open: preset
  D_Flip_Flop d_ff_8 (.D(d_ff_8_qn), .clk(d_ff_7_qn), .Q(COUNT[7]), .Qn(d_ff_8_qn), .reset(RST));  // open: preset
  D_Flip_Flop d_ff_9 (.D(d_ff_9_qn), .clk(d_ff_8_qn), .Q(COUNT[8]), .Qn(d_ff_9_qn), .reset(RST));  // open: preset
  D_Flip_Flop d_ff_10 (.D(OVF), .clk(d_ff_9_qn), .Q(COUNT[9]), .Qn(OVF), .reset(RST));  // open: preset
endmodule

module custom_counter_4 (
  input  CLK,
  input  RST,
  output [3:0] COUNT
);

  wire d_ff_1_qn, d_ff_2_qn, d_ff_3_qn, d_ff_4_qn;

  D_Flip_Flop d_ff_1 (.D(d_ff_1_qn), .clk(CLK), .Q(COUNT[0]), .Qn(d_ff_1_qn), .reset(RST));  // open: preset
  D_Flip_Flop d_ff_2 (.D(d_ff_2_qn), .clk(d_ff_1_qn), .Q(COUNT[1]), .Qn(d_ff_2_qn), .reset(RST));  // open: preset
  D_Flip_Flop d_ff_3 (.D(d_ff_3_qn), .clk(d_ff_2_qn), .Q(COUNT[2]), .Qn(d_ff_3_qn), .reset(RST));  // open: preset
  D_Flip_Flop d_ff_4 (.D(d_ff_4_qn), .clk(d_ff_3_qn), .Q(COUNT[3]), .Qn(d_ff_4_qn), .reset(RST));  // open: preset
endmodule

module custom_counter_3 (
  input  CLK,
  input  RST,
  output [2:0] COUNT
);

  wire d_ff_1_qn, d_ff_2_qn, d_ff_3_qn;

  D_Flip_Flop d_ff_1 (.D(d_ff_1_qn), .clk(CLK), .Q(COUNT[0]), .Qn(d_ff_1_qn), .reset(RST));  // open: preset
  D_Flip_Flop d_ff_2 (.D(d_ff_2_qn), .clk(d_ff_1_qn), .Q(COUNT[1]), .Qn(d_ff_2_qn), .reset(RST));  // open: preset
  D_Flip_Flop d_ff_3 (.D(d_ff_3_qn), .clk(d_ff_2_qn), .Q(COUNT[2]), .Qn(d_ff_3_qn), .reset(RST));  // open: preset
endmodule

module test (
);

  wire clock_1_out, d_ff_1_q, d_ff_1_qn, d_ff_2_q, d_ff_2_qn, main_1_a, main_1_b, main_1_c, main_1_d,
       main_1_e, main_1_f, main_1_g, main_1_sel, switch_1_p2;

  // Switch switch_1: pin names not known; wires that end beside it: 1'b1, switch_1_p2
  Clock clock_1 (.out(clock_1_out));
  Pull_Resistor pull_resistor_1 (.node(switch_1_p2));
  main main_1 (
    .CLK(clock_1_out), .RST(switch_1_p2), .A(main_1_a), .B(main_1_b), .C(main_1_c), .D(main_1_d),
    .E(main_1_e), .F(main_1_f), .G(main_1_g), .SEL(main_1_sel));
  D_Flip_Flop d_ff_1 (.D(d_ff_1_qn), .clk(main_1_sel), .Q(d_ff_1_q), .Qn(d_ff_1_qn));  // open: preset, reset
  D_Flip_Flop d_ff_2 (.D(d_ff_2_qn), .clk(d_ff_1_qn), .Q(d_ff_2_q), .Qn(d_ff_2_qn));  // open: preset, reset
  _7_Segment_Display u_7_segment_display_1 (
    .g(main_1_g), .f(main_1_f), .a(main_1_a), .b(main_1_b), .e(main_1_e), .d(main_1_d), .c(main_1_c),
    .dp(1'b1));
  LED led_1 (.in(d_ff_1_q));
  LED led_2 (.in(d_ff_2_q));
endmodule
